// Logisim project s-mips.circ as structural Verilog: 22 circuits, main circuit S-MIPS Board
module S_MIPS_Board (
  input  DESHABILITAR_DISPATCHER,
  output halt
);

  wire button_1_out, CLK, CS, d_ff_1_q, LCLR, LoadRAM, LoadRAMOn, LW, R_R_W, R_W, ram_dispatcher_1_finished,
       RCS, Reset_out, RST, TTY_EN;
  wire [2:0] KDB;
  wire [3:0] LMask, Mask, ram_1_read_time, ram_1_write_time, RMask;
  wire [6:0] KDB_DATA, TTY_DATA;
  wire [15:0] Addr, LAddr, RAddr;
  wire [31:0] I0, I1, I2, I3, LData, ram_1_data_out_0, ram_1_data_out_1, ram_1_data_out_2, ram_1_data_out_3,
       RI0, RI1, RI2, RI3;

  TTY #(.rows(25), .cols(80)) tty_1 (.data(TTY_DATA), .clk(CLK), .we(TTY_EN), .clr(RST));
  not not_1 (LoadRAMOn, ram_dispatcher_1_finished);
  RAM_Dispatcher ram_dispatcher_1 (
    .WriteTime(ram_1_write_time), .Clock(CLK), .Data(LData), .Address(LAddr), .Mask(LMask),
    .Finished(ram_dispatcher_1_finished), .Write(LW), .CLR(LCLR));
  Keyboard #(.buflen(64)) keyboard_1 (.clk(CLK), .re(KDB[0]), .avail(KDB[2]), .data(KDB_DATA));  // open: clr
  RAM ram_1 (
    .Address(RAddr), .Data_Out_0(ram_1_data_out_0), .Data_Out_1(ram_1_data_out_1),
    .Data_Out_2(ram_1_data_out_2), .Data_Out_3(ram_1_data_out_3), .Data_In_0(RI0), .Data_In_1(RI1),
    .Data_In_2(RI2), .Data_In_3(RI3), .Mask(RMask), .nRead_Write(R_R_W), .Chip_Select(RCS),
    .Read_Time(ram_1_read_time), .Reset(button_1_out), .Write_Time(ram_1_write_time));
  Button button_1 (.out(button_1_out));
  D_Flip_Flop d_ff_1 (.clk(CLK), .D(1'b1), .Q(d_ff_1_q), .reset(Reset_out));  // open: Qn, preset, en
  Button Reset (.out(Reset_out));
  S_MIPS s_mips_1 (
    .Kbd_Enable(KDB[0]), .Address(Addr), .Kbd_Clear(KDB[1]), .Kbd_Available(KDB[2]), .RAM_In_0(I0),
    .Kbd_ASCII_Data(KDB_DATA), .RAM_In_1(I1), .TTY_Enable(TTY_EN), .RAM_In_2(I2), .RAM_In_3(I3),
    .TTY_ASCII_Data(TTY_DATA), .Reset(RST), .RAM_Out_0(ram_1_data_out_0), .Clock(CLK),
    .RAM_Out_1(ram_1_data_out_1), .Stop(halt), .RAM_Out_2(ram_1_data_out_2), .RAM_Out_3(ram_1_data_out_3),
    .Mask(Mask), .Read_Time(ram_1_read_time), .Write_Time(ram_1_write_time), .nRead_Write(R_W),
    .Chip_Select(CS));
  D_Flip_Flop d_ff_2 (.clk(CLK), .D(d_ff_1_q), .Qn(LCLR), .reset(Reset_out));  // open: Q, preset, en
  or or_1 (RST, LCLR, LoadRAM);
  Clock clock_1 (.out(CLK));
  Multiplexer #(.width(32), .enable("false")) multiplexer_1 (.in0(I0), .in1(LData), .out(RI0), .sel(LoadRAM));
  Multiplexer #(.width(32), .enable("false")) multiplexer_2 (.in0(I1), .in1(LData), .out(RI1), .sel(LoadRAM));
  Multiplexer #(.width(32), .enable("false")) multiplexer_3 (.in0(I2), .in1(LData), .out(RI2), .sel(LoadRAM));
  Multiplexer #(.width(32), .enable("false")) multiplexer_4 (.in0(I3), .in1(LData), .out(RI3), .sel(LoadRAM));
  and and_1 (LoadRAM, ~DESHABILITAR_DISPATCHER, LoadRAMOn);  // AND_Gate
  Multiplexer #(.width(16), .enable("false")) multiplexer_5 (.in0(Addr), .in1(LAddr), .out(RAddr), .sel(LoadRAM));
  Multiplexer #(.width(4), .enable("false")) multiplexer_6 (.in0(Mask), .in1(LMask), .out(RMask), .sel(LoadRAM));
  Multiplexer #(.enable("false")) multiplexer_7 (.in0(CS), .in1(LW), .out(RCS), .sel(LoadRAM));
  Multiplexer #(.enable("false")) multiplexer_8 (.in0(R_W), .in1(LW), .out(R_R_W), .sel(LoadRAM));

  // Notes on the sheet:
  //   NO MODIFICAR
  //   Keyboard
endmodule

module RAM (
  input  [15:0] Address,
  input  [31:0] Data_In_0,
  input  [31:0] Data_In_1,
  input  [31:0] Data_In_2,
  input  [31:0] Data_In_3,
  input  [3:0] Mask,
  input  nRead_Write,
  input  Chip_Select,
  input  Reset,
  output [31:0] Data_Out_0,
  output [31:0] Data_Out_1,
  output [31:0] Data_Out_2,
  output [31:0] Data_Out_3,
  output [3:0] Read_Time,
  output [3:0] Write_Time
);

  wire and_2_out, and_3_out, and_4_out, and_5_out, and_6_out, and_7_out, and_8_out, and_9_out, Changed, CLK,
       comparator_2_eq, comparator_3_eq, comparator_4_eq, comparator_5_eq, comparator_6_eq, Count,
       demultiplexer_3_out0, Idle, Idle_q, Load, Load0, Load1, nand_1_out, or_1_out, or_2_out, or_3_out,
       or_4_out, or_5_out, or_6_out, or_7_out, or_8_out, or_9_out, or_10_out, Proc_q, Update_Mem, Zero_Time;
  wire [3:0] counter_1_q, multiplexer_1_out, subtractor_1_out;
  wire [31:0] register_1_q, register_2_q, register_3_q, register_4_q, register_5_q;

  // Probe on 4'b0011
  // Probe on 4'b0010
  Multiplexer #(.width(4), .enable("false")) multiplexer_1 (
    .in0(4'b0011), .in1(4'b0010), .out(multiplexer_1_out), .sel(nRead_Write));
  or or_1 (or_1_out, Idle, Update_Mem);
  or or_2 (or_2_out, ~Chip_Select, Reset);  // OR_Gate
  Subtractor #(.width(4)) subtractor_1 (.a(multiplexer_1_out), .b(4'b0010), .out(subtractor_1_out));  // open: bin, bout
  Demultiplexer #(.enable("false")) demultiplexer_1 (.out0(Idle), .out1(Load0), .in(Idle_q), .sel(Changed));
  D_Flip_Flop u_Idle (.clk(CLK), .D(or_1_out), .Q(Idle_q), .preset(or_2_out));  // open: Qn, en, reset
  // Probe on counter_1_q
  Counter #(.width(4), .max('hf)) counter_1 (
    .load(Load), .D(subtractor_1_out), .count(Count), .Q(counter_1_q), .clk(CLK), .clr(or_3_out));  // open: carry
  or or_3 (or_3_out, ~Chip_Select, Reset);  // OR_Gate
  Comparator #(.width(4), .mode("unsigned")) comparator_1 (
    .a(4'b0000), .b(counter_1_q), .eq(Zero_Time));  // open: gt, lt
  or or_4 (or_4_out, Count, Load0, Load1);
  Register #(.width(32)) register_1 (.D(Data_In_0), .en(Chip_Select), .Q(register_1_q), .clk(CLK), .clr(or_5_out));
  or or_5 (or_5_out, ~Chip_Select, Reset);  // OR_Gate
  Register #(.width(32)) register_2 (.D(Data_In_1), .en(Chip_Select), .Q(register_2_q), .clk(CLK), .clr(or_6_out));
  or or_6 (or_6_out, ~Chip_Select, Reset);  // OR_Gate
  Register #(.width(32)) register_3 (.D(Data_In_2), .en(Chip_Select), .Q(register_3_q), .clk(CLK), .clr(or_7_out));
  or or_7 (or_7_out, ~Chip_Select, Reset);  // OR_Gate
  Register #(.width(32)) register_4 (.D(Data_In_3), .en(Chip_Select), .Q(register_4_q), .clk(CLK), .clr(or_8_out));
  or or_8 (or_8_out, ~Chip_Select, Reset);  // OR_Gate
  Register #(.width(32)) register_5 (
    .D({{11{1'b1}}, nRead_Write, Mask, Address}), .en(Chip_Select), .Q(register_5_q), .clk(CLK),
    .clr(or_9_out));
  or or_9 (or_9_out, ~Chip_Select, Reset);  // OR_Gate
  D_Flip_Flop Proc (.clk(CLK), .D(or_4_out), .Q(Proc_q), .reset(or_10_out));  // open: Qn, preset, en
  or or_10 (or_10_out, ~Chip_Select, Reset);  // OR_Gate
  Demultiplexer #(.enable("false")) demultiplexer_2 (
    .out0(Count), .out1(Update_Mem), .in(demultiplexer_3_out0), .sel(Zero_Time));
  Demultiplexer #(.enable("false")) demultiplexer_3 (
    .out0(demultiplexer_3_out0), .out1(Load1), .in(Proc_q), .sel(Changed));
  Clock clock_1 (.out(CLK));
  Comparator #(.width(32)) comparator_2 (.a(register_1_q), .b(Data_In_0), .eq(comparator_2_eq));  // open: gt, lt
  Comparator #(.width(32)) comparator_3 (.a(register_2_q), .b(Data_In_1), .eq(comparator_3_eq));  // open: gt, lt
  Comparator #(.width(32)) comparator_4 (.a(register_3_q), .b(Data_In_2), .eq(comparator_4_eq));  // open: gt, lt
  Comparator #(.width(32)) comparator_5 (.a(register_4_q), .b(Data_In_3), .eq(comparator_5_eq));  // open: gt, lt
  Comparator #(.width(32)) comparator_6 (
    .a(register_5_q), .b({{11{1'b1}}, nRead_Write, Mask, Address}), .eq(comparator_6_eq));  // open: gt, lt
  nand nand_1 (nand_1_out, comparator_6_eq, comparator_2_eq, comparator_3_eq, comparator_4_eq, comparator_5_eq);
  and and_1 (Changed, nand_1_out, Chip_Select);
  or or_11 (Load, Count, Load1, Load0);
  and and_2 (and_2_out, Mask[0], Update_Mem, nRead_Write);
  and and_3 (and_3_out, Mask[1], Update_Mem, nRead_Write);
  and and_4 (and_4_out, Mask[2], Update_Mem, nRead_Write);
  and and_5 (and_5_out, Mask[3], Update_Mem, nRead_Write);
  RAM_part #(.addrWidth(16), .dataWidth(32), .bus("separate")) ram_1 (
    .addr(Address), .din(Data_In_0), .data(Data_Out_0), .str(and_2_out), .sel(Chip_Select), .clk(CLK),
    .ld(and_6_out), .clr(Reset));
  and and_6 (and_6_out, ~nRead_Write, Idle);  // AND_Gate
  RAM_part #(.addrWidth(16), .dataWidth(32), .bus("separate")) ram_2 (
    .addr(Address), .din(Data_In_1), .data(Data_Out_1), .str(and_3_out), .sel(Chip_Select), .clk(CLK),
    .ld(and_7_out), .clr(Reset));
  and and_7 (and_7_out, ~nRead_Write, Idle);  // AND_Gate
  RAM_part #(.addrWidth(16), .dataWidth(32), .bus("separate")) ram_3 (
    .addr(Address), .din(Data_In_2), .data(Data_Out_2), .str(and_4_out), .sel(Chip_Select), .clk(CLK),
    .ld(and_8_out), .clr(Reset));
  and and_8 (and_8_out, ~nRead_Write, Idle);  // AND_Gate
  RAM_part #(.addrWidth(16), .dataWidth(32), .bus("separate")) ram_4 (
    .addr(Address), .din(Data_In_3), .data(Data_Out_3), .str(and_5_out), .sel(Chip_Select), .clk(CLK),
    .ld(and_9_out), .clr(Reset));
  and and_9 (and_9_out, ~nRead_Write, Idle);  // AND_Gate

  assign Read_Time = 4'b0011;
  assign Write_Time = 4'b0010;

  // Other names for the same wires on the sheet: M0 = Mask[0]; M1 = Mask[1]; M2 = Mask[2]; M3 = Mask[3];
  //   RW = nRead_Write; CLR = Reset; CS = Chip_Select; Load2 = Count

  // Notes on the sheet:
  //   NO MODIFICAR
  //   excepto quizás los valores RT y WT
  //   BANK0
  //   BANK1
  //   BANK2
  //   BANK3
endmodule

module S_MIPS (
  input  Kbd_Available,
  input  [6:0] Kbd_ASCII_Data,
  input  [31:0] RAM_Out_0,
  input  [31:0] RAM_Out_1,
  input  Reset,
  input  [31:0] RAM_Out_2,
  input  Clock,
  input  [31:0] RAM_Out_3,
  input  [3:0] Read_Time,
  input  [3:0] Write_Time,
  output Kbd_Enable,
  output [15:0] Address,
  output Kbd_Clear,
  output TTY_Enable,
  output [6:0] TTY_ASCII_Data,
  output Stop,
  output [31:0] RAM_In_0,
  output [31:0] RAM_In_1,
  output [31:0] RAM_In_2,
  output [31:0] RAM_In_3,
  output [3:0] Mask,
  output nRead_Write,
  output Chip_Select
);

  wire cambio, d_ff_1_qn, done, falling_edge_high_1_out, falling_edge_high_2_out, memory_reader_1_util,
       not_1_out, not_2_out, reset_t, rising_edge_high_1_out, Run;
  wire [31:0] Address_t, datapath_1_ram_address, demultiplexer_1_out0, Instruction, memory_reader_1_from_ram,
       RAM;

  D_Flip_Flop #(.trigger("falling")) d_ff_1 (
    .clk(Clock), .Qn(d_ff_1_qn), .preset(Clock), .en(d_ff_1_qn));  // open: D, Q, reset
  Falling_Edge_High falling_edge_high_1 (.in(d_ff_1_qn), .out(falling_edge_high_1_out));
  or or_1 (reset_t, falling_edge_high_1_out, cambio);
  DataPath datapath_1 (
    .Instruction(Instruction), .Run(Run), .CLK(Clock), .reset(Reset), .KBD_DATA(Kbd_ASCII_Data),
    .KBD_AVAIL(Kbd_Available), .RAM_entry(RAM), .TTY_ENABLE(TTY_Enable), .TTY_DATA(TTY_ASCII_Data),
    .Stop(Stop), .RAM_Address(datapath_1_ram_address));
  D_Flip_Flop #(.trigger("falling")) d_ff_2 (
    .Q(Chip_Select), .preset(reset_t), .reset(rising_edge_high_1_out));  // open: clk, D, Qn, en
  not not_1 (not_1_out, memory_reader_1_util);
  Memory_Reader memory_reader_1 (
    .Address(Address_t), .From_RAM_1(RAM_Out_1), .From_RAM_2(RAM_Out_2), .From_RAM_3(RAM_Out_3),
    .RT(Read_Time), .CLK(Clock), .reset(reset_t), .RAM_Address(Address), .From_RAM(memory_reader_1_from_ram),
    .Util(memory_reader_1_util), .From_RAM_0(RAM_Out_0));
  Demultiplexer #(.width(32), .enable("false")) demultiplexer_1 (
    .out0(demultiplexer_1_out0), .out1(RAM), .in(memory_reader_1_from_ram), .sel(Run));
  Register #(.width(32)) register_1 (.D(datapath_1_ram_address), .Q(Address_t), .clr(Run));  // open: en, clk
  D_Flip_Flop #(.trigger("falling")) d_ff_3 (
    .Q(Run), .preset(falling_edge_high_2_out), .reset(done));  // open: clk, D, Qn, en
  Falling_Edge_High falling_edge_high_2 (.in(Chip_Select), .out(falling_edge_high_2_out));
  Rising_Edge_High rising_edge_high_1 (.in(not_1_out), .out(rising_edge_high_1_out));
  not not_2 (not_2_out, Run);
  Falling_Edge_High falling_edge_high_3 (.in(Run), .out(cambio));
  Register #(.width(32)) register_2 (.D(demultiplexer_1_out0), .Q(Instruction), .clr(not_2_out));  // open: en, clk

  assign Kbd_Clear = 1'b0;
  assign Kbd_Enable = 1'b0;
  assign nRead_Write = 1'b0;

  // Other names for the same wires on the sheet: CLK = Clock; CLR = Reset; KBD_AVAIL = Kbd_Available;
  //   KBD_DATA[6:0] = Kbd_ASCII_Data; RAM_A[15:0] = Address; RAM_INPUT_0[31:0] = RAM_In_0;
  //   RAM_INPUT_1[31:0] = RAM_In_1; RAM_INPUT_2[31:0] = RAM_In_2; RAM_INPUT_3[31:0] = RAM_In_3; RAM_MASK[3:0] = Mask;
  //   RAM_OUTPUT_0[31:0] = RAM_Out_0; RAM_OUTPUT_1[31:0] = RAM_Out_1; RAM_OUTPUT_2[31:0] = RAM_Out_2;
  //   RAM_OUTPUT_3[31:0] = RAM_Out_3; CS = Chip_Select; Read = Chip_Select; TTY_DATA[6:0] = TTY_ASCII_Data

  // Notes on the sheet:
  //   RAM ADDRESS
  //   DATA FROM RAM
  //   DATA TO RAM
  //   DATA WRITE MASK
  //   RAM TIMING
  //   RAM CONTROL
  //   KEYBOARD
  //   TTY
  //   SEQUENCING
endmodule

module RAM_Dispatcher (
  input  [3:0] WriteTime,
  input  Clock,
  input  CLR,
  output [31:0] Data,
  output [15:0] Address,
  output [3:0] Mask,
  output Finished,
  output Write
);

  wire demultiplexer_2_out1, demultiplexer_3_out1, End, IDLE_q, IncAddr, Load, or_1_out, or_2_out, While_q,
       WriteEnd;
  wire [3:0] counter_1_q;
  wire [31:0] CurrentAddress_q;

  Counter #(.width(32), .max('hffffffff)) CurrentAddress (
    .count(IncAddr), .Q({CurrentAddress_q[31:18], Address, CurrentAddress_q[1:0]}), .clk(Clock), .clr(CLR));  // open: load, D, carry
  or or_1 (or_1_out, IncAddr, demultiplexer_3_out1, Finished);
  D_Flip_Flop IDLE (.clk(Clock), .D(or_1_out), .Q(IDLE_q), .preset(CLR));  // open: Qn, en, reset
  Demultiplexer #(.enable("false")) demultiplexer_1 (.out0(Load), .out1(Finished), .in(IDLE_q), .sel(End));
  D_Flip_Flop While (.clk(Clock), .D(or_2_out), .Q(While_q), .reset(CLR));  // open: Qn, preset, en
  or or_2 (or_2_out, Write, Load);
  RAM_part #(.addrWidth(18), .dataWidth(32)) ram_1 (
    .addr({Address, CurrentAddress_q[1:0]}), .data(Data), .clk(Clock));  // open: sel, ld, clr
  Demultiplexer #(.enable("false")) demultiplexer_2 (
    .out0(Write), .out1(demultiplexer_2_out1), .in(While_q), .sel(WriteEnd));
  Decoder #(.select(2)) decoder_1 (
    .out0(Mask[0]), .out1(Mask[1]), .out2(Mask[2]), .out3(Mask[3]), .sel(CurrentAddress_q[1:0]));  // open: en
  Demultiplexer #(.enable("false")) demultiplexer_3 (
    .out0(IncAddr), .out1(demultiplexer_3_out1), .in(demultiplexer_2_out1), .sel(End));
  Counter #(.width(4), .max('hf)) counter_1 (
    .load(Load), .D(WriteTime), .count(Write), .Q(counter_1_q), .clk(Clock));  // open: carry, clr
  Comparator #(.width(32)) comparator_1 (.a(Data), .b({32{1'b1}}), .eq(End));  // open: gt, lt
  Comparator #(.width(4)) comparator_2 (.a(4'b0000), .b(counter_1_q), .eq(WriteEnd));  // open: gt, lt

  // Other names for the same wires on the sheet: CLK = Clock; Count = Write; WT[3:0] = WriteTime
endmodule

// 32
module Register_File (
  input  push,
  input  Clock,
  input  pop,
  input  R_W,
  input  [4:0] Destination_Address,
  input  [31:0] Input,
  input  [4:0] Selector_A,
  input  [4:0] Selector_B,
  input  Reset,
  output [31:0] Output_A,
  output [31:0] Output_B,
  output [31:0] SP
);

  wire demultiplexer_1_out31, or_2_out, W1, W2, W3, W4, W5, W6, W7, W8, W9, W10, W11, W12, W13, W14, W15,
       W16, W17, W18, W19, W20, W21, W22, W23, W24, W25, W26, W27, W28, W29, W30, W31;
  wire [31:0] adder_1_out, multiplexer_3_out, multiplexer_4_out, R1, R2, R3, R4, R5, R6, R7, R8, R9, R10,
       R11, R12, R13, R14, R15, R16, R17, R18, R19, R20, R21, R22, R23, R24, R25, R26, R27, R28, R29, R30;

  Demultiplexer #(.select(5), .disabled(0)) demultiplexer_1 (
    .out1(W1), .out2(W2), .out3(W3), .out4(W4), .out5(W5), .out6(W6), .out7(W7), .out8(W8), .out9(W9),
    .out10(W10), .out11(W11), .out12(W12), .out13(W13), .out14(W14), .out15(W15), .out16(W16), .out17(W17),
    .out18(W18), .out19(W19), .out20(W20), .out21(W21), .out22(W22), .out23(W23), .out24(W24), .out25(W25),
    .out26(W26), .out27(W27), .out28(W28), .out29(W29), .out30(W30), .out31(demultiplexer_1_out31),
    .in(1'b1), .sel(Destination_Address), .en(R_W));  // open: out0
  or or_1 (W31, demultiplexer_1_out31, push, pop);
  Register #(.width(32)) register_1 (.D(Input), .en(W1), .Q(R1), .clk(Clock), .clr(Reset));
  Register #(.width(32)) register_2 (.D(Input), .en(W9), .Q(R9), .clk(Clock), .clr(Reset));
  Register #(.width(32)) register_3 (.D(Input), .en(W17), .Q(R17), .clk(Clock), .clr(Reset));
  Register #(.width(32)) register_4 (.D(Input), .en(W25), .Q(R25), .clk(Clock), .clr(Reset));
  Multiplexer #(.select(5), .width(32), .enable("false")) multiplexer_1 (
    .in0({32{1'b0}}), .in1(R1), .in2(R2), .in3(R3), .in4(R4), .in5(R5), .in6(R6), .in7(R7), .in8(R8),
    .in9(R9), .in10(R10), .in11(R11), .in12(R12), .in13(R13), .in14(R14), .in15(R15), .in16(R16), .in17(R17),
    .in18(R18), .in19(R19), .in20(R20), .in21(R21), .in22(R22), .in23(R23), .in24(R24), .in25(R25),
    .in26(R26), .in27(R27), .in28(R28), .in29(R29), .in30(R30), .in31(SP), .out(Output_A), .sel(Selector_A));
  Register #(.width(32)) register_5 (.D(Input), .en(W2), .Q(R2), .clk(Clock), .clr(Reset));
  Register #(.width(32)) register_6 (.D(Input), .en(W10), .Q(R10), .clk(Clock), .clr(Reset));
  Register #(.width(32)) register_7 (.D(Input), .en(W18), .Q(R18), .clk(Clock), .clr(Reset));
  Register #(.width(32)) register_8 (.D(Input), .en(W26), .Q(R26), .clk(Clock), .clr(Reset));
  // Probe on Output_A
  // Probe on Output_B
  // Probe on SP
  Register #(.width(32)) register_9 (.D(Input), .en(W3), .Q(R3), .clk(Clock), .clr(Reset));
  Register #(.width(32)) register_10 (.D(Input), .en(W11), .Q(R11), .clk(Clock), .clr(Reset));
  Register #(.width(32)) register_11 (.D(Input), .en(W19), .Q(R19), .clr(Reset));  // open: clk
  Register #(.width(32)) register_12 (.D(Input), .en(W27), .Q(R27), .clk(Clock), .clr(Reset));
  Multiplexer #(.select(5), .width(32), .enable("false")) multiplexer_2 (
    .in0({32{1'b0}}), .in1(R1), .in2(R2), .in3(R3), .in4(R4), .in5(R5), .in6(R6), .in7(R7), .in8(R8),
    .in9(R9), .in10(R10), .in11(R11), .in12(R12), .in13(R13), .in14(R14), .in15(R15), .in16(R16), .in17(R17),
    .in18(R18), .in19(R19), .in20(R20), .in21(R21), .in22(R22), .in23(R23), .in24(R24), .in25(R25),
    .in26(R26), .in27(R27), .in28(R28), .in29(R29), .in30(R30), .in31(SP), .out(Output_B), .sel(Selector_B));
  Register #(.width(32)) register_13 (.D(Input), .en(W4), .Q(R4), .clk(Clock), .clr(Reset));
  Register #(.width(32)) register_14 (.D(Input), .en(W12), .Q(R12), .clk(Clock), .clr(Reset));
  Register #(.width(32)) register_15 (.D(Input), .en(W20), .Q(R20), .clk(Clock), .clr(Reset));
  Register #(.width(32)) register_16 (.D(Input), .en(W28), .Q(R28), .clk(Clock), .clr(Reset));
  Multiplexer #(.width(32), .disabled(0), .enable("false")) multiplexer_3 (
    .in0(32'h4), .in1(32'hfffffffc), .out(multiplexer_3_out), .sel(push));
  Register #(.width(32)) register_17 (.D(Input), .en(W5), .Q(R5), .clk(Clock), .clr(Reset));
  Register #(.width(32)) register_18 (.D(Input), .en(W13), .Q(R13), .clk(Clock), .clr(Reset));
  Register #(.width(32)) register_19 (.D(Input), .en(W21), .Q(R21), .clk(Clock), .clr(Reset));
  Register #(.width(32)) register_20 (.D(Input), .en(W29), .Q(R29), .clk(Clock), .clr(Reset));
  Adder #(.width(32)) adder_1 (.a(SP), .b(multiplexer_3_out), .out(adder_1_out));  // open: cin, cout
  or or_2 (or_2_out, push, pop);
  Register #(.width(32)) register_21 (.D(Input), .en(W6), .Q(R6), .clk(Clock), .clr(Reset));
  Register #(.width(32)) register_22 (.D(Input), .en(W14), .Q(R14), .clk(Clock), .clr(Reset));
  Register #(.width(32)) register_23 (.D(Input), .en(W22), .Q(R22), .clk(Clock), .clr(Reset));
  Register #(.width(32)) register_24 (.D(Input), .en(W30), .Q(R30), .clk(Clock), .clr(Reset));
  Multiplexer #(.width(32), .enable("false")) multiplexer_4 (
    .in0(Input), .in1(adder_1_out), .out(multiplexer_4_out), .sel(or_2_out));
  Register #(.width(32)) register_25 (.D(Input), .en(W7), .Q(R7));  // open: clk, clr
  Register #(.width(32)) register_26 (.D(Input), .en(W15), .Q(R15), .clk(Clock), .clr(Reset));
  Register #(.width(32)) register_27 (.D(Input), .en(W23), .Q(R23), .clk(Clock), .clr(Reset));
  Register #(.width(32)) register_28 (.D(multiplexer_4_out), .en(W31), .Q(SP), .clk(Clock), .clr(Reset));
  Register #(.width(32)) register_29 (.D(Input), .en(W8), .Q(R8), .clk(Clock), .clr(Reset));
  Register #(.width(32)) register_30 (.D(Input), .en(W16), .Q(R16), .clk(Clock), .clr(Reset));
  Register #(.width(32)) register_31 (.D(Input), .en(W24), .Q(R24), .clk(Clock), .clr(Reset));

  // Other names for the same wires on the sheet: CLK = Clock; Data[31:0] = Input; Dest[4:0] = Destination_Address;
  //   OA[31:0] = Output_A; OB[31:0] = Output_B; R31[31:0] = SP; SA[4:0] = Selector_A; SB[4:0] = Selector_B
endmodule

module Instruction_Decoder (
  input  [31:0] Instruction,
  output [4:0] Rd,
  output [4:0] Rt,
  output [25:0] Address,
  output [4:0] Rs,
  output [5:0] OpCode,
  output [5:0] FuncCode,
  output [15:0] Inmediate,
  output [3:0] FS,
  output [1:0] ALU_input,
  output Tipo_I,
  output W_ALU,
  output W_RF,
  output nop,
  output pop,
  output push,
  output add,
  output KBD,
  output tty,
  output jr,
  output rnd,
  output mfhi,
  output halt,
  output sub,
  output mflo,
  output mult,
  output \and ,
  output mulu,
  output bltz,
  output \or ,
  output beq,
  output div,
  output bne,
  output \xor ,
  output blez,
  output divu,
  output \nor ,
  output addi,
  output slt,
  output slti,
  output sltu,
  output sltiu,
  output andi,
  output ori,
  output bgtz,
  output xori,
  output Branch,
  output Unsigned_Extension,
  output sw,
  output lw,
  output j
);

  wire _0_opC, comparator_2_eq, comparator_3_eq, Tipo_R;

  Comparator #(.width(6)) comparator_1 (.a(Instruction[31:26]), .b({6{1'b0}}), .eq(_0_opC));  // open: gt, lt
  Comparator #(.width(6)) comparator_2 (.a(Instruction[31:26]), .b(6'b101110), .eq(comparator_2_eq));  // open: gt, lt
  Comparator #(.width(6)) comparator_3 (.a(Instruction[31:26]), .b(6'b110101), .eq(comparator_3_eq));  // open: gt, lt
  Comparator #(.width(6)) comparator_4 (.a(Instruction[31:26]), .b(6'b000010), .eq(j));  // open: gt, lt
  or or_1 (Tipo_R, _0_opC, comparator_3_eq);
  nor nor_1 (Tipo_I, Tipo_R, j);
  assign FS = j ? 4'b0000 : 4'bz;  // Controlled_Buffer controlled_buffer_1
  nor nor_2 (W_RF, Branch, j, jr, sw, push);
  _0_opC_Decoder u_0_opc_decoder_1 (
    .FuncCode(Instruction[31:26]), ._0_opC(_0_opC), .nop(nop), .add(add), .jr(jr), .mfhi(mfhi), .sub(sub),
    .mflo(mflo), .mult(mult), .\and (\and ), .FS(FS), .multu(mulu), .\or (\or ), .div(div), .\xor (\xor ),
    .divu(divu), .\nor (\nor ), .slt(slt), .sltu(sltu), .W_ALU(W_ALU));
  other_R_Decoder other_r_decoder_1 (
    .FuncCode(Instruction[5:0]), .OpCode(Instruction[31:26]), .pop(pop), .push(push), .KBD(KBD), .tty(tty),
    .rnd(rnd), .halt(halt), .FS(FS));
  I_type_Decoder i_type_decoder_1 (
    .OpCode(Instruction[31:26]), .Tipo_I(Tipo_I), .FS(FS), .beq(beq), .bne(bne), .lw(lw), .sw(sw),
    .bltz(bltz), .blez(blez), .addi(addi), .slti(slti), .sltiu(sltiu), .andi(andi), .ori(ori), .xori(xori),
    .ALU_input(ALU_input), .Branch(Branch), .bgtz(bgtz));  // open: Enable
  or or_2 (Unsigned_Extension, andi, ori, xori);

  assign Address = {Instruction[15:11], Instruction[20:0]};
  assign FuncCode = Instruction[5:0];
  assign Inmediate = Instruction[15:0];
  assign OpCode = Instruction[31:26];
  assign Rd = Instruction[15:11];
  assign Rs = Instruction[25:21];
  assign Rt = Instruction[20:16];

  // Other names for the same wires on the sheet: Shamt[4:0] = Instruction[10:6]
endmodule

module Program_Counter (
  input  CLK,
  input  reset,
  input  branch,
  input  j,
  input  jr,
  input  Condition,
  input  [15:0] offset,
  input  [25:0] Address,
  input  [31:0] RA,
  output [31:0] OPC
);

  wire or_1_out, or_2_out;
  wire [31:0] adder_1_out, adder_2_out, IPC, multiplexer_2_out, multiplexer_3_out;

  Adder #(.width(32)) adder_1 (.a(OPC), .b(32'h4), .out(adder_1_out));  // open: cin, cout
  Adder #(.width(32)) adder_2 (.a(adder_1_out), .b({2'b00, offset, {14{1'b0}}}), .out(adder_2_out));  // open: cin, cout
  or or_1 (or_1_out, branch, Condition);
  Multiplexer #(.width(32), .enable("false")) multiplexer_1 (
    .in0({OPC[31:28], Address, 2'b00}), .in1(RA), .out(IPC), .sel(jr));
  Multiplexer #(.width(32), .enable("false")) multiplexer_2 (
    .in0(adder_1_out), .in1(adder_2_out), .out(multiplexer_2_out), .sel(or_1_out));
  or or_2 (or_2_out, jr, j);
  Multiplexer #(.width(32), .enable("false")) multiplexer_3 (
    .in0(multiplexer_2_out), .in1(IPC), .out(multiplexer_3_out), .sel(or_2_out));
  Register #(.width(32)) register_1 (.D(multiplexer_3_out), .en(1'b1), .Q(OPC), .clk(CLK), .clr(reset));

  // Other names for the same wires on the sheet: Cond = Condition
endmodule

module Complemento_2 (
  input  [31:0] A,
  output [31:0] B
);

  wire [31:0] not_1_out;

  assign not_1_out = ~A;  // NOT_Gate not_1, 32 bits wide
  Adder #(.width(32)) adder_1 (.a(32'h1), .b(not_1_out), .out(B));  // open: cin, cout
endmodule

module Complemento_2_64_bits (
  input  [31:0] Hi,
  input  [31:0] Lo,
  output [31:0] Hi_2,
  output [31:0] Lo_2
);

  wire adder_1_cout;
  wire [31:0] not_1_out, not_2_out;

  assign not_1_out = ~Hi;  // NOT_Gate not_1, 32 bits wide
  assign not_2_out = ~Lo;  // NOT_Gate not_2, 32 bits wide
  Adder #(.width(32)) adder_1 (.a(32'h1), .b(not_2_out), .out(Lo_2), .cout(adder_1_cout));  // open: cin
  Adder #(.width(32)) adder_2 (.a({32{1'b0}}), .b(not_1_out), .out(Hi_2), .cin(adder_1_cout));  // open: cout
endmodule

module Multiplicador (
  input  [31:0] A,
  input  [31:0] B,
  input  \signed ,
  output [31:0] Hi,
  output [31:0] Lo
);

  wire and_1_out, xor_1_out;
  wire [31:0] complemento_2_1_b, complemento_2_2_b, complemento_2_64_bits_1_hi_2,
       complemento_2_64_bits_1_lo_2, multiplexer_1_out, multiplexer_2_out, multiplier_1_cout,
       multiplier_1_out;

  // Probe on A
  // Probe on B
  Complemento_2 complemento_2_1 (.A(A), .B(complemento_2_1_b));
  Complemento_2 complemento_2_2 (.A(B), .B(complemento_2_2_b));
  Multiplexer #(.width(32), .enable("false")) multiplexer_1 (
    .in0(A), .in1(complemento_2_1_b), .out(multiplexer_1_out), .sel(A[31]));
  Multiplexer #(.width(32), .enable("false")) multiplexer_2 (
    .in0(B), .in1(complemento_2_2_b), .out(multiplexer_2_out), .sel(B[31]));
  // Probe on Hi
  // Probe on Lo
  Multiplier #(.width(32)) multiplier_1 (
    .a(multiplexer_1_out), .b(multiplexer_2_out), .out(multiplier_1_out), .cout(multiplier_1_cout));  // open: cin
  Complemento_2_64_bits complemento_2_64_bits_1 (
    .Hi(multiplier_1_cout), .Lo(multiplier_1_out), .Hi_2(complemento_2_64_bits_1_hi_2),
    .Lo_2(complemento_2_64_bits_1_lo_2));
  Multiplexer #(.width(32), .enable("false")) multiplexer_3 (
    .in0(multiplier_1_cout), .in1(complemento_2_64_bits_1_hi_2), .out(Hi), .sel(and_1_out));
  Multiplexer #(.width(32), .enable("false")) multiplexer_4 (
    .in0(multiplier_1_out), .in1(complemento_2_64_bits_1_lo_2), .out(Lo), .sel(and_1_out));
  and and_1 (and_1_out, \signed , xor_1_out);
  xor xor_1 (xor_1_out, A[31], B[31]);

  // Other names for the same wires on the sheet: SignA = A[31]; SignB = B[31]
endmodule

module Divisor (
  input  [31:0] A,
  input  [31:0] B,
  input  \signed ,
  output [31:0] Hi,
  output [31:0] Lo
);

  wire and_1_out, or_1_out, xor_1_out;
  wire [1:1] and_2_out;
  wire [31:0] adder_1_out, complemento_2_1_b, complemento_2_2_b, complemento_2_3_b, divider_1_out,
       divider_1_rem, multiplexer_1_out, multiplexer_2_out, multiplexer_4_out, subtractor_1_out,
       subtractor_2_out;

  // Probe on A
  // Probe on B
  Complemento_2 complemento_2_1 (.A(A), .B(complemento_2_1_b));
  Complemento_2 complemento_2_2 (.A(B), .B(complemento_2_2_b));
  Multiplexer #(.width(32), .enable("false")) multiplexer_1 (
    .in0(A), .in1(complemento_2_1_b), .out(multiplexer_1_out), .sel(A[31]));
  Multiplexer #(.width(32), .enable("false")) multiplexer_2 (
    .in0(B), .in1(complemento_2_2_b), .out(multiplexer_2_out), .sel(B[31]));
  // Probe on Hi
  // Probe on Lo
  Divider #(.width(32)) divider_1 (
    .a(multiplexer_1_out), .b(multiplexer_2_out), .out(divider_1_out), .rem(divider_1_rem));  // open: upper
  Subtractor #(.width(32)) subtractor_1 (
    .a(multiplexer_2_out), .b(divider_1_rem), .out(subtractor_1_out));  // open: bin, bout
  Complemento_2 complemento_2_3 (.A(divider_1_out), .B(complemento_2_3_b));
  and and_1 (and_1_out, \signed , or_1_out);
  Multiplexer #(.width(32), .enable("false")) multiplexer_3 (
    .in0(divider_1_rem), .in1(subtractor_1_out), .out(Hi), .sel(and_1_out));
  Multiplexer #(.width(32), .enable("false")) multiplexer_4 (
    .in0(divider_1_out), .in1(complemento_2_3_b), .out(multiplexer_4_out), .sel(and_2_out[1]));
  and and_2 (and_2_out[1], \signed , xor_1_out);
  xor xor_1 (xor_1_out, A[31], B[31]);
  or or_1 (or_1_out, A[31], B[31]);
  Subtractor #(.width(32)) subtractor_2 (.a(multiplexer_4_out), .b(32'h1), .out(subtractor_2_out));  // open: bin, bout
  Adder #(.width(32)) adder_1 (.a(multiplexer_4_out), .b(32'h1), .out(adder_1_out));  // open: cin, cout
  Multiplexer #(.select(2), .width(32), .enable("false")) multiplexer_5 (
    .in0(multiplexer_4_out), .in1(adder_1_out), .in2(subtractor_2_out), .in3(subtractor_2_out), .out(Lo),
    .sel({and_2_out[1], B[31]}));

  // Other names for the same wires on the sheet: SignB = B[31]; SignA = A[31]
endmodule

module ALU (
  input  [31:0] A,
  input  [31:0] B,
  input  [3:0] FS,
  input  Write,
  input  CLK,
  input  Reset,
  output [31:0] Out
);

  wire comparator_1_gt, comparator_1_lt, comparator_2_eq, comparator_2_gt, comparator_2_lt, Enable, not_2_out;
  wire [31:0] adder_1_out, and_2_out, bit_extender_1_out, bit_extender_2_out, bit_extender_3_out,
       bit_extender_4_out, bit_extender_5_out, bit_extender_6_out, divisor_1_hi, divisor_1_lo,
       multiplexer_1_out, multiplexer_2_out, multiplicador_1_hi, multiplicador_1_lo, not_1_out, or_1_out,
       or_2_out, register_1_q, register_2_q, subtractor_1_out, xor_1_out;

  and and_1 (Enable, FS[3], Write, FS[2]);
  Adder #(.width(32)) adder_1 (.a(A), .b(B), .out(adder_1_out));  // open: cin, cout
  Subtractor #(.width(32)) subtractor_1 (.a(A), .b(B), .out(subtractor_1_out));  // open: bin, bout
  assign or_1_out = A | B;  // OR_Gate or_1, 32 bits wide
  assign and_2_out = A & B;  // AND_Gate and_2, 32 bits wide
  assign xor_1_out = A ^ B;  // XOR_Gate xor_1, 32 bits wide
  Comparator #(.width(32)) comparator_1 (.a(A), .b(B), .gt(comparator_1_gt), .lt(comparator_1_lt));  // open: eq
  Comparator #(.width(32), .mode("unsigned")) comparator_2 (
    .a(A), .b(B), .gt(comparator_2_gt), .eq(comparator_2_eq), .lt(comparator_2_lt));
  Multiplicador multiplicador_1 (.A(A), .B(B), .\signed (FS[1]), .Hi(multiplicador_1_hi), .Lo(multiplicador_1_lo));
  Divisor divisor_1 (.A(A), .B(B), .\signed (FS[1]), .Hi(divisor_1_hi), .Lo(divisor_1_lo));
  assign not_1_out = ~or_1_out;  // NOT_Gate not_1, 32 bits wide
  assign bit_extender_1_out = {{31{1'b0}}, comparator_1_gt};  // Bit_Extender bit_extender_1
  assign bit_extender_2_out = {{31{1'b0}}, comparator_1_lt};  // Bit_Extender bit_extender_2
  assign bit_extender_3_out = {{31{1'b0}}, comparator_2_gt};  // Bit_Extender bit_extender_3
  assign bit_extender_4_out = {{31{1'b0}}, comparator_2_lt};  // Bit_Extender bit_extender_4
  assign bit_extender_5_out = {{31{1'b0}}, comparator_2_eq};  // Bit_Extender bit_extender_5
  Multiplexer #(.width(32), .enable("false")) multiplexer_1 (
    .in0(multiplicador_1_hi), .in1(divisor_1_hi), .out(multiplexer_1_out), .sel(FS[0]));
  Multiplexer #(.width(32), .enable("false")) multiplexer_2 (
    .in0(multiplicador_1_lo), .in1(divisor_1_lo), .out(multiplexer_2_out), .sel(FS[0]));
  assign or_2_out = bit_extender_2_out | bit_extender_5_out;  // OR_Gate or_2, 32 bits wide
  assign bit_extender_6_out = {{31{1'b0}}, not_2_out};  // Bit_Extender bit_extender_6
  not not_2 (not_2_out, comparator_2_eq);
  Register #(.width(32)) register_1 (.D(multiplexer_1_out), .en(Enable), .Q(register_1_q), .clk(CLK), .clr(Reset));
  Register #(.width(32)) register_2 (.D(multiplexer_2_out), .en(Enable), .Q(register_2_q), .clk(CLK), .clr(Reset));
  Multiplexer #(.select(4), .width(32), .enable("false")) multiplexer_3 (
    .in0(adder_1_out), .in1(subtractor_1_out), .in2(or_1_out), .in3(not_1_out), .in4(and_2_out),
    .in5(xor_1_out), .in6(bit_extender_1_out), .in7(bit_extender_2_out), .in8(bit_extender_3_out),
    .in9(bit_extender_4_out), .in10(bit_extender_5_out), .in12(or_2_out), .in13(bit_extender_6_out),
    .in14(register_1_q), .in15(register_2_q), .out(Out), .sel(FS));  // open: in11
  // Probe on Out
  // Probe on A
  // Probe on B

  // Other names for the same wires on the sheet: M_D = FS[0]
endmodule

module _0_opC_Decoder (
  input  [5:0] FuncCode,
  input  _0_opC,
  output nop,
  output add,
  output jr,
  output mfhi,
  output sub,
  output mflo,
  output mult,
  output \and ,
  output [3:0] FS,
  output multu,
  output \or ,
  output div,
  output \xor ,
  output divu,
  output \nor ,
  output slt,
  output sltu,
  output W_ALU
);

  wire comparator_1_eq, comparator_2_eq, comparator_3_eq, comparator_4_eq, comparator_5_eq, comparator_6_eq,
       comparator_7_eq, comparator_8_eq, comparator_9_eq, comparator_10_eq, comparator_11_eq,
       comparator_12_eq, comparator_13_eq, comparator_14_eq, comparator_15_eq, comparator_16_eq, or_1_out,
       or_2_out;
  wire [3:0] or_3_out;

  Comparator #(.width(6), .mode("unsigned")) comparator_1 (
    .a(FuncCode), .b({6{1'b0}}), .eq(comparator_1_eq));  // open: gt, lt
  Comparator #(.width(6), .mode("unsigned")) comparator_2 (
    .a(FuncCode), .b(6'b001000), .eq(comparator_2_eq));  // open: gt, lt
  Comparator #(.width(6), .mode("unsigned")) comparator_3 (
    .a(FuncCode), .b(6'b010000), .eq(comparator_3_eq));  // open: gt, lt
  Comparator #(.width(6), .mode("unsigned")) comparator_4 (
    .a(FuncCode), .b(6'b010010), .eq(comparator_4_eq));  // open: gt, lt
  Comparator #(.width(6), .mode("unsigned")) comparator_5 (
    .a(FuncCode), .b(6'b011000), .eq(comparator_5_eq));  // open: gt, lt
  Comparator #(.width(6), .mode("unsigned")) comparator_6 (
    .a(FuncCode), .b(6'b011001), .eq(comparator_6_eq));  // open: gt, lt
  Comparator #(.width(6), .mode("unsigned")) comparator_7 (
    .a(FuncCode), .b(6'b011010), .eq(comparator_7_eq));  // open: gt, lt
  Comparator #(.width(6), .mode("unsigned")) comparator_8 (
    .a(FuncCode), .b(6'b011011), .eq(comparator_8_eq));  // open: gt, lt
  and and_1 (nop, comparator_1_eq, _0_opC);
  and and_2 (jr, comparator_2_eq, _0_opC);
  and and_3 (mfhi, comparator_3_eq, _0_opC);
  and and_4 (mflo, comparator_4_eq, _0_opC);
  and and_5 (mult, comparator_5_eq, _0_opC);
  and and_6 (multu, comparator_6_eq, _0_opC);
  and and_7 (div, comparator_7_eq, _0_opC);
  and and_8 (divu, comparator_8_eq, _0_opC);
  Comparator #(.width(6), .mode("unsigned")) comparator_9 (
    .a(FuncCode), .b(6'b100000), .eq(comparator_9_eq));  // open: gt, lt
  Comparator #(.width(6), .mode("unsigned")) comparator_10 (
    .a(FuncCode), .b(6'b100010), .eq(comparator_10_eq));  // open: gt, lt
  Comparator #(.width(6), .mode("unsigned")) comparator_11 (
    .a(FuncCode), .b(6'b100100), .eq(comparator_11_eq));  // open: gt, lt
  Comparator #(.width(6), .mode("unsigned")) comparator_12 (
    .a(FuncCode), .b(6'b100101), .eq(comparator_12_eq));  // open: gt, lt
  Comparator #(.width(6), .mode("unsigned")) comparator_13 (
    .a(FuncCode), .b(6'b100110), .eq(comparator_13_eq));  // open: gt, lt
  Comparator #(.width(6), .mode("unsigned")) comparator_14 (
    .a(FuncCode), .b(6'b100111), .eq(comparator_14_eq));  // open: gt, lt
  Comparator #(.width(6), .mode("unsigned")) comparator_15 (
    .a(FuncCode), .b(6'b101010), .eq(comparator_15_eq));  // open: gt, lt
  Comparator #(.width(6), .mode("unsigned")) comparator_16 (
    .a(FuncCode), .b(6'b101011), .eq(comparator_16_eq));  // open: gt, lt
  and and_9 (add, comparator_9_eq, _0_opC);
  buf and_10 (sub, comparator_10_eq);  // AND_Gate
  and and_11 (\and , comparator_11_eq, _0_opC);
  and and_12 (\or , comparator_12_eq, _0_opC);
  and and_13 (\xor , comparator_13_eq, _0_opC);
  and and_14 (\nor , comparator_14_eq, _0_opC);
  and and_15 (slt, comparator_15_eq, _0_opC);
  and and_16 (sltu, comparator_16_eq, _0_opC);
  or or_1 (or_1_out, mult, mfhi);
  or or_2 (or_2_out, div, mflo);
  or or_3 (or_3_out[0], or_2_out, slt, \xor , sub, \nor , sltu, divu);
  or or_4 (or_3_out[1], or_2_out, or_1_out, \nor , \nor , \or , slt);
  or or_5 (or_3_out[2], multu, or_2_out, \and , slt, \xor , or_1_out, divu);
  or or_6 (or_3_out[3], multu, sltu, or_2_out, or_1_out, divu);
  or or_7 (W_ALU, divu, div, mult, multu);
  assign FS = _0_opC ? or_3_out : 4'bz;  // Controlled_Buffer controlled_buffer_1

  // Other names for the same wires on the sheet: mul = mult; mulu = multu
endmodule

module other_R_Decoder (
  input  [5:0] FuncCode,
  input  [5:0] OpCode,
  output [3:0] FS,
  output pop,
  output push,
  output KBD,
  output tty,
  output rnd,
  output halt
);

  wire comparator_1_eq, comparator_2_eq;

  Demultiplexer #(.enable("false")) demultiplexer_1 (.out0(pop), .out1(push), .in(comparator_1_eq), .sel(FuncCode[0]));
  Comparator #(.width(6), .mode("unsigned")) comparator_1 (
    .a(OpCode), .b(6'b111000), .eq(comparator_1_eq));  // open: gt, lt
  Comparator #(.width(6), .mode("unsigned")) comparator_2 (
    .a(OpCode), .b({6{1'b1}}), .eq(comparator_2_eq));  // open: gt, lt
  Demultiplexer #(.select(2), .enable("false")) demultiplexer_2 (
    .out0(KBD), .out1(tty), .out2(rnd), .out3(halt), .in(comparator_2_eq), .sel(FuncCode[1:0]));

  assign FS = 4'b0000;

  // Other names for the same wires on the sheet: _2LSB[1:0] = FuncCode[1:0]; LSB = FuncCode[0]
endmodule

module I_type_Decoder (
  input  Tipo_I,
  input  [5:0] OpCode,
  input  Enable,
  output addi,
  output bltz,
  output slti,
  output beq,
  output sltiu,
  output bne,
  output andi,
  output [3:0] FS,
  output blez,
  output ori,
  output bgtz,
  output xori,
  output lw,
  output Branch,
  output sw,
  output [1:0] ALU_input
);

  wire comparator_12_eq, comparator_13_eq, or_1_out, or_2_out, or_4_out;
  wire [3:0] or_5_out;

  Comparator #(.width(6), .mode("unsigned")) comparator_1 (.a(OpCode), .b(6'b000001), .eq(bltz));  // open: gt, lt
  Comparator #(.width(6), .mode("unsigned")) comparator_2 (.a(OpCode), .b(6'b000100), .eq(beq));  // open: gt, lt
  Comparator #(.width(6), .mode("unsigned")) comparator_3 (.a(OpCode), .b(6'b000101), .eq(bne));  // open: gt, lt
  Comparator #(.width(6), .mode("unsigned")) comparator_4 (.a(OpCode), .b(6'b000110), .eq(blez));  // open: gt, lt
  Comparator #(.width(6), .mode("unsigned")) comparator_5 (.a(OpCode), .b(6'b000111), .eq(bgtz));  // open: gt, lt
  or or_1 (or_1_out, bltz, blez, bgtz);
  or or_2 (or_2_out, addi, andi, slti, sltiu, ori, xori);
  or or_3 (Branch, beq, bne, or_1_out);
  Priority_Encoder #(.select(2)) priority_encoder_1 (
    .in0(1'b1), .in1(or_1_out), .in2(or_2_out), .out(ALU_input));  // open: in3, gs, en_out, en_in
  Comparator #(.width(6), .mode("unsigned")) comparator_6 (.a(OpCode), .b(6'b001000), .eq(addi));  // open: gt, lt
  Comparator #(.width(6), .mode("unsigned")) comparator_7 (.a(OpCode), .b(6'b001010), .eq(slti));  // open: gt, lt
  Comparator #(.width(6), .mode("unsigned")) comparator_8 (.a(OpCode), .b(6'b001011), .eq(sltiu));  // open: gt, lt
  Comparator #(.width(6), .mode("unsigned")) comparator_9 (.a(OpCode), .b(6'b001100), .eq(andi));  // open: gt, lt
  Comparator #(.width(6), .mode("unsigned")) comparator_10 (.a(OpCode), .b(6'b001101), .eq(ori));  // open: gt, lt
  Comparator #(.width(6), .mode("unsigned")) comparator_11 (.a(OpCode), .b(6'b001110), .eq(xori));  // open: gt, lt
  Comparator #(.width(6), .mode("unsigned")) comparator_12 (
    .a(OpCode), .b(6'b100011), .eq(comparator_12_eq));  // open: gt, lt
  Comparator #(.width(6), .mode("unsigned")) comparator_13 (
    .a(OpCode), .b(6'b101011), .eq(comparator_13_eq));  // open: gt, lt
  and and_1 (lw, comparator_12_eq, Enable);
  and and_2 (sw, comparator_13_eq, Enable);
  or or_4 (or_4_out, bltz, slti);
  or or_5 (or_5_out[0], or_4_out, sltiu, xori, bne);
  or or_6 (or_5_out[1], or_4_out, ori, bgtz, beq);
  or or_7 (or_5_out[2], or_4_out, andi, xori, blez, bne, bgtz);
  or or_8 (or_5_out[3], blez, sltiu, bne, beq);
  assign FS = Tipo_I ? or_5_out : 4'bz;  // Controlled_Buffer controlled_buffer_1
endmodule

module DataPath (
  input  [31:0] Instruction,
  input  Run,
  input  CLK,
  input  reset,
  input  [6:0] KBD_DATA,
  input  KBD_AVAIL,
  input  [31:0] RAM_entry,
  output TTY_ENABLE,
  output [6:0] TTY_DATA,
  output Stop,
  output [31:0] RAM_Address
);

  wire Branch, Charge_Ins, j, jr, KBD, lw, pop, push, Queue_Ins, rnd, sw, Tipo_I, U_Ext, W_ALU, W_RF;
  wire [1:0] ALU_input, or_2_out;
  wire [3:0] FS;
  wire [4:0] multiplexer_4_out, Rd, Rs, Rt;
  wire [15:0] Inmediate;
  wire [25:0] Addres, Address;
  wire [31:0] ALU, bit_extender_1_out, bit_extender_2_out, bit_extender_3_out, bit_extender_4_out,
       multiplexer_1_out, multiplexer_2_out, multiplexer_3_out, multiplexer_5_out, PC, random_1_out, Rt_t, SP;
  wire [31:7] Rs_t;

  assign bit_extender_1_out = {{16{Inmediate[15]}}, Inmediate};  // Bit_Extender bit_extender_1
  assign bit_extender_2_out = {{16{1'b0}}, Inmediate};  // Bit_Extender bit_extender_2
  Random #(.width(32)) random_1 (.clk(CLK), .out(random_1_out));  // open: next, clr
  Multiplexer #(.width(32), .enable("false")) multiplexer_1 (
    .in0(bit_extender_1_out), .in1(bit_extender_2_out), .out(multiplexer_1_out), .sel(U_Ext));
  Multiplexer #(.width(32), .enable("false")) multiplexer_2 (
    .in0(32'h1), .in1(bit_extender_3_out), .out(multiplexer_2_out), .sel(KBD_AVAIL));
  assign bit_extender_3_out = {{25{1'b0}}, KBD_DATA};  // Bit_Extender bit_extender_3
  Multiplexer #(.select(2), .width(32), .enable("false")) multiplexer_3 (
    .in0(Rt_t), .in1({32{1'b0}}), .in2(multiplexer_1_out), .out(multiplexer_3_out), .sel(ALU_input));  // open: in3
  Multiplexer #(.width(5), .enable("false")) multiplexer_4 (.in0(Rd), .in1(Rt), .out(multiplexer_4_out), .sel(Tipo_I));
  Multiplexer #(.select(2), .width(32), .enable("false")) multiplexer_5 (
    .in0(ALU), .in1(RAM_entry), .in2(random_1_out), .in3(multiplexer_2_out), .out(multiplexer_5_out),
    .sel(or_2_out));
  or or_1 (or_2_out[1], KBD, rnd);
  or or_2 (or_2_out[0], push, lw, KBD);
  ALU alu_1 (.A({Rs_t, TTY_DATA}), .B(multiplexer_3_out), .FS(FS), .Write(W_ALU), .CLK(CLK), .Reset(reset), .Out(ALU));
  Register_File register_file_1 (
    .push(push), .Clock(CLK), .pop(pop), .R_W(W_RF), .Destination_Address(multiplexer_4_out),
    .Input(multiplexer_5_out), .Selector_A(Rs), .Selector_B(Rt), .Reset(reset), .Output_A({Rs_t, TTY_DATA}),
    .Output_B(Rt_t), .SP(SP));
  Instruction_Decoder instruction_decoder_1 (
    .Rd(Rd), .Rt(Rt), .Address(Addres), .Rs(Rs), .Inmediate(Inmediate), .FS(FS), .pop(pop), .push(push),
    .KBD(KBD), .jr(jr), .tty(TTY_ENABLE), .rnd(rnd), .halt(Stop), .j(j), .lw(lw), .sw(sw), .Branch(Branch),
    .ALU_input(ALU_input), .Unsigned_Extension(U_Ext), .W_ALU(W_ALU), .W_RF(W_RF), .Tipo_I(Tipo_I),
    .Instruction(Instruction));  // open: OpCode, FuncCode, nop, add, mfhi, sub, mflo, bltz, mult, beq, and, blez, mulu, or, addi, div, xor, sltiu, divu, andi, nor, ori, slt, xori, sltu, bgtz, bne, slti
  Program_Counter program_counter_1 (
    .CLK(CLK), .reset(reset), .branch(Branch), .j(j), .jr(jr), .Condition(ALU[0]), .offset(Inmediate),
    .Address(Address), .RA({Rs_t, TTY_DATA}), .OPC(PC));
  assign bit_extender_4_out = {{16{Inmediate[15]}}, Inmediate};  // Bit_Extender bit_extender_4
  Multiplexer #(.select(2), .width(32), .enable("false")) multiplexer_6 (
    .in0(PC), .in1(SP), .in2(bit_extender_4_out), .out(RAM_Address), .sel({Charge_Ins, Queue_Ins}));  // open: in3
  or or_3 (Charge_Ins, lw, sw);
  or or_4 (Queue_Ins, push, pop);
  Multiplexer #(.width(32), .enable("false")) multiplexer_7 (
    .in0({32{1'b0}}), .in1({Instruction[7:0], Instruction[15:8], Instruction[23:16], Instruction[31:24]}),
    .sel(Run));  // open: out

  // Other names for the same wires on the sheet: RAM[31:0] = RAM_entry; Rs_t[6:0] = TTY_DATA
endmodule

module Memory_Writer (
  input  [31:0] Data,
  input  [31:0] Address,
  input  [3:0] Write_Time,
  input  CLK,
  input  Clear,
  output [15:0] RAM_Address,
  output [31:0] To_RAM_0,
  output [31:0] To_RAM_1,
  output Ready,
  output [31:0] To_RAM_2,
  output [31:0] To_RAM_3,
  output [3:0] Mask
);

  wire [3:0] counter_1_q;

  Demultiplexer #(.select(2), .width(32), .disabled(0), .enable("false")) demultiplexer_1 (
    .out0(To_RAM_0), .out1(To_RAM_1), .out2(To_RAM_2), .out3(To_RAM_3), .in(Data), .sel(Address[3:2]));
  Counter #(.width(4), .max('hf)) counter_1 (.Q(counter_1_q), .clk(CLK), .clr(Clear));  // open: load, D, count, carry
  Comparator #(.width(4), .mode("unsigned")) comparator_1 (
    .a(Write_Time), .b(counter_1_q), .eq(Ready));  // open: gt, lt
  Decoder #(.select(2), .enable("false")) decoder_1 (
    .out0(Mask[0]), .out1(Mask[1]), .out2(Mask[2]), .out3(Mask[3]), .sel(Address[3:2]));

  assign RAM_Address = Address[19:4];

  // Other names for the same wires on the sheet: Block[1:0] = Address[3:2]
endmodule

module Memory_Reader (
  input  [31:0] Address,
  input  [31:0] From_RAM_0,
  input  [31:0] From_RAM_1,
  input  [31:0] From_RAM_2,
  input  [31:0] From_RAM_3,
  input  [3:0] RT,
  input  CLK,
  input  reset,
  output [15:0] RAM_Address,
  output [31:0] From_RAM,
  output Util
);

  wire and_1_out, comparator_1_gt, falling_edge_low_1_out;
  wire [3:0] counter_1_q;

  Comparator #(.width(4), .mode("unsigned")) comparator_1 (
    .a(RT), .b(counter_1_q), .gt(comparator_1_gt));  // open: eq, lt
  Counter #(.width(4), .max('hf)) counter_1 (.Q(counter_1_q), .clk(CLK), .clr(reset));  // open: load, D, count, carry
  Multiplexer #(.select(2), .width(32), .enable("false")) multiplexer_1 (
    .in0(From_RAM_0), .in1(From_RAM_1), .in2(From_RAM_2), .in3(From_RAM_3), .out(From_RAM), .sel(Address[3:2]));
  Falling_Edge__Low falling_edge_low_1 (.in(comparator_1_gt), .out(falling_edge_low_1_out));
  and and_1 (and_1_out, falling_edge_low_1_out, Util);
  or or_1 (Util, reset, and_1_out);

  assign RAM_Address = Address[19:4];

  // Other names for the same wires on the sheet: byte[1:0] = Address[1:0]; Block[1:0] = Address[3:2]
endmodule

module Control_Unit (
  input  CLK,
  input  done,
  output Read,
  output Run
);

  wire cambio, d_ff_1_qn, falling_edge_high_1_out, falling_edge_high_2_out, memory_reader_1_util, not_1_out,
       reset, rising_edge_high_1_out;

  D_Flip_Flop #(.trigger("falling")) d_ff_1 (
    .clk(CLK), .Qn(d_ff_1_qn), .preset(CLK), .en(d_ff_1_qn));  // open: D, Q, reset
  Falling_Edge_High falling_edge_high_1 (.in(d_ff_1_qn), .out(falling_edge_high_1_out));
  or or_1 (reset, falling_edge_high_1_out, cambio);
  D_Flip_Flop #(.trigger("falling")) d_ff_2 (
    .Q(Read), .preset(reset), .reset(rising_edge_high_1_out));  // open: clk, D, Qn, en
  Rising_Edge_High rising_edge_high_1 (.in(not_1_out), .out(rising_edge_high_1_out));
  not not_1 (not_1_out, memory_reader_1_util);
  Memory_Reader memory_reader_1 (
    .RT(4'b0011), .CLK(CLK), .reset(reset), .Util(memory_reader_1_util));  // open: Address, From_RAM_1, From_RAM_2, From_RAM_3, RAM_Address, From_RAM, From_RAM_0
  D_Flip_Flop #(.trigger("falling")) d_ff_3 (
    .Q(Run), .preset(falling_edge_high_2_out), .reset(done));  // open: clk, D, Qn, en
  Falling_Edge_High falling_edge_high_2 (.in(Read), .out(falling_edge_high_2_out));
  Falling_Edge_High falling_edge_high_3 (.in(Run), .out(cambio));
endmodule

// FEL
module Falling_Edge__Low (
  input  in,
  output out
);

  wire not_1_out, not_2_out, not_3_out;

  not not_1 (not_1_out, in);
  or or_1 (out, in, not_3_out);
  not not_2 (not_2_out, not_1_out);
  not not_3 (not_3_out, not_2_out);
endmodule

// FEH
module Falling_Edge_High (
  input  in,
  output out
);

  wire falling_edge_low_1_out;

  Falling_Edge__Low falling_edge_low_1 (.in(in), .out(falling_edge_low_1_out));
  not not_1 (out, falling_edge_low_1_out);
endmodule

// REH
module Rising_Edge_High (
  input  in,
  output out
);

  wire falling_edge_low_1_out, not_1_out;

  not not_1 (not_1_out, in);
  not not_2 (out, falling_edge_low_1_out);
  Falling_Edge__Low falling_edge_low_1 (.in(not_1_out), .out(falling_edge_low_1_out));
endmodule
